// Logisim project bcd.circ as structural Verilog: 1 circuit, main circuit implementation
module implementation (
  input  w3,
  input  w2,
  input  w1,
  input  w0,
  output a,
  output b,
  output c,
  output d,
  output e,
  output f,
  output g
);

  wire not_w0, not_w1, not_w2, not_w3, nw1_AND_nw0, nw2_AND_nw0, nw2_AND_w1, w1_AND_nw0, w1_AND_w0,
       w2_AND_nw0, w2_AND_nw1, w2_AND_nw1_AND_w0, w2_AND_w0;

  and and_1 (nw2_AND_nw0, not_w2, not_w0);
  and and_2 (nw1_AND_nw0, not_w1, not_w0);
  not not_1 (not_w3, w3);
  not not_2 (not_w2, w2);
  not not_3 (not_w1, w1);
  not not_4 (not_w0, w0);
  or or_1 (a, w3, w1, nw2_AND_nw0, w2_AND_w0);
  or or_2 (e, nw2_AND_nw0, w1_AND_nw0);
  and and_3 (w2_AND_w0, w2, w0);
  and and_4 (w1_AND_w0, w1, w0);
  or or_3 (b, not_w2, nw1_AND_nw0, w1_AND_w0);
  or or_4 (f, w3, nw1_AND_nw0, w2_AND_nw1, w2_AND_nw0);
  and and_5 (w1_AND_nw0, w1, not_w0);
  and and_6 (nw2_AND_w1, not_w2, w1);
  and and_7 (w2_AND_nw1, w2, not_w1);
  and and_8 (w2_AND_nw0, w2, not_w0);
  or or_5 (c, not_w1, w0, w2);
  or or_6 (g, w3, w2_AND_nw1, nw2_AND_w1, w1_AND_nw0);
  and and_9 (w2_AND_nw1_AND_w0, w2, not_w1, w0);
  or or_7 (d, w3, w1_AND_nw0, nw2_AND_nw0, nw2_AND_w1, w2_AND_nw1_AND_w0);

  // Other names for the same wires on the sheet: at = a; bt = b; ct = c; dt = d; et = e; ft = f; gt = g; w0t = w0;
  //   w1t = w1; w2t = w2; w3t = w3
endmodule
