// Logisim project fun.circ as structural Verilog: 1 circuit, main circuit implementation
module implementation (
  input  x3,
  input  x2,
  input  x1,
  input  x0,
  output the_output
);

  wire x0_AND_x1, x2_AND_x3;

  and and_1 (x0_AND_x1, x1, x0);
  and and_2 (x2_AND_x3, x3, x2);
  or or_1 (the_output, x0_AND_x1, x2_AND_x3);

  // Other names for the same wires on the sheet: the_output_t = the_output; x0t = x0; x1t = x1; x2t = x2; x3t = x3
endmodule
