// Logisim project adder4.circ as structural Verilog: 1 circuit, main circuit implementation
module implementation (
  input  [3:0] Ain,
  input  [3:0] Bin,
  input  Cinin,
  output [3:0] Sum_Out,
  output Carry_Out
);

  wire and_5_out, and_6_out, and_7_out, and_8_out, and_9_out, and_10_out, and_11_out, and_12_out, and_13_out,
       and_14_out, C0, C1, C2, G0, G1, G2, G3, P0, P1, P2, P3;

  and and_1 (G0, Ain[0], Bin[0]);
  or or_1 (P0, Ain[0], Bin[0]);
  and and_2 (G1, Ain[1], Bin[1]);
  or or_2 (P1, Ain[1], Bin[1]);
  and and_3 (G2, Ain[2], Bin[2]);
  or or_3 (P2, Ain[2], Bin[2]);
  and and_4 (G3, Ain[3], Bin[3]);
  or or_4 (P3, Ain[3], Bin[3]);
  // Probe on Ain
  // Probe on Bin
  and and_5 (and_5_out, Cinin, P0);
  or or_5 (C0, and_5_out, G0);
  and and_6 (and_6_out, Cinin, P0, P1);
  or or_6 (C1, and_6_out, and_7_out, G1);
  and and_7 (and_7_out, G0, P1);
  and and_8 (and_8_out, Cinin, P0, P1, P2);
  and and_9 (and_9_out, G0, P1, P2);
  or or_7 (C2, and_8_out, and_9_out, and_10_out, G2);
  and and_10 (and_10_out, G1, P2);
  and and_11 (and_11_out, Cinin, P0, P1, P2, P3);
  and and_12 (and_12_out, G0, P1, P2, P3);
  and and_13 (and_13_out, G1, P2, P3);
  and and_14 (and_14_out, G2, P3);
  or or_8 (Carry_Out, and_11_out, and_12_out, and_13_out, and_14_out, G3);
  xor xor_1 (Sum_Out[0], Ain[0], Bin[0], Cinin);
  xor xor_2 (Sum_Out[1], Ain[1], Bin[1], C0);
  xor xor_3 (Sum_Out[2], Ain[2], Bin[2], C1);
  xor xor_4 (Sum_Out[3], Ain[3], Bin[3], C2);

  // Other names for the same wires on the sheet: A[3:0] = Ain; A_0 = Ain[0]; A_1 = Ain[1]; A_2 = Ain[2]; A_3 = Ain[3];
  //   B[3:0] = Bin; B_0 = Bin[0]; B_1 = Bin[1]; B_2 = Bin[2]; B_3 = Bin[3]; C3 = Carry_Out; Cin = Cinin;
  //   S_0 = Sum_Out[0]; Sum[3:0] = Sum_Out; S_1 = Sum_Out[1]; S_2 = Sum_Out[2]; S_3 = Sum_Out[3]
endmodule
