// Logisim project bitcounter.circ as structural Verilog: 1 circuit, main circuit implementation
module implementation (
  input  [7:0] BitsIn,
  input  CountZerosIn,
  output [3:0] BitCountOut
);

  wire adder_1_cout, adder_1_out, adder_2_cout, adder_2_out, adder_3_cout, adder_3_out, adder_4_cout,
       adder_4_out, adder_5_cout, adder_5_out, adder_6_cout, adder_6_out, adder_7_cout, adder_7_out,
       adder_8_cout, adder_8_out, adder_9_cout, adder_10_cout;
  wire [7:0] multiplexer_1_out, negator_1_out, subtractor_1_out;

  Negator negator_1 (.in(BitsIn), .out(negator_1_out));
  Subtractor subtractor_1 (.a(negator_1_out), .b(8'h1), .out(subtractor_1_out));  // open: bin, bout
  Multiplexer #(.enable("false"), .width(8)) multiplexer_1 (
    .in0(BitsIn), .in1(subtractor_1_out), .out(multiplexer_1_out), .sel(CountZerosIn));
  Adder #(.width(1)) adder_1 (
    .a(multiplexer_1_out[0]), .b(multiplexer_1_out[1]), .out(adder_1_out), .cout(adder_1_cout));  // open: cin
  Adder #(.width(1)) adder_2 (
    .a(multiplexer_1_out[2]), .b(multiplexer_1_out[3]), .out(adder_2_out), .cout(adder_2_cout));  // open: cin
  Adder #(.width(1)) adder_3 (
    .a(multiplexer_1_out[4]), .b(multiplexer_1_out[5]), .out(adder_3_out), .cout(adder_3_cout));  // open: cin
  Adder #(.width(1)) adder_4 (
    .a(multiplexer_1_out[6]), .b(multiplexer_1_out[7]), .out(adder_4_out), .cout(adder_4_cout));  // open: cin
  Adder #(.width(1)) adder_5 (.a(adder_1_out), .b(adder_2_out), .out(adder_5_out), .cout(adder_5_cout));  // open: cin
  Adder #(.width(1)) adder_6 (
    .a(adder_1_cout), .b(adder_2_cout), .out(adder_6_out), .cin(adder_5_cout), .cout(adder_6_cout));
  Adder #(.width(1)) adder_7 (.a(adder_3_out), .b(adder_4_out), .out(adder_7_out), .cout(adder_7_cout));  // open: cin
  Adder #(.width(1)) adder_8 (
    .a(adder_3_cout), .b(adder_4_cout), .out(adder_8_out), .cin(adder_7_cout), .cout(adder_8_cout));
  Adder #(.width(1)) adder_9 (
    .a(adder_5_out), .b(adder_7_out), .out(BitCountOut[0]), .cout(adder_9_cout));  // open: cin
  Adder #(.width(1)) adder_10 (
    .a(adder_6_out), .b(adder_8_out), .out(BitCountOut[1]), .cin(adder_9_cout), .cout(adder_10_cout));
  Adder #(.width(1)) adder_11 (
    .a(adder_6_cout), .b(adder_8_cout), .out(BitCountOut[2]), .cin(adder_10_cout), .cout(BitCountOut[3]));

  // Other names for the same wires on the sheet: BitCount[3:0] = BitCountOut; Bits[7:0] = BitsIn;
  //   CountZeros = CountZerosIn
endmodule
