// Logisim project shifter.circ as structural Verilog: 1 circuit, main circuit implementation
module implementation (
  input  IsRightShiftIn,
  input  IsArithmeticIn,
  input  [1:0] ShiftAmountIn,
  input  [2:0] NumberIn,
  output [2:0] ShiftedNumberOut
);

  wire RightFill;
  wire [2:0] multiplexer_2_out, multiplexer_5_out;

  Multiplexer #(.enable("false")) multiplexer_1 (.in0(1'b0), .in1(NumberIn[2]), .out(RightFill), .sel(IsArithmeticIn));
  Multiplexer #(.enable("false"), .select(2)) multiplexer_2 (
    .in0(NumberIn[0]), .in1(1'b0), .in2(1'b0), .in3(1'b0), .out(multiplexer_2_out[0]), .sel(ShiftAmountIn));
  Multiplexer #(.enable("false"), .select(2)) multiplexer_3 (
    .in0(NumberIn[1]), .in1(NumberIn[0]), .in2(1'b0), .in3(1'b0), .out(multiplexer_2_out[1]),
    .sel(ShiftAmountIn));
  Multiplexer #(.enable("false"), .select(2)) multiplexer_4 (
    .in0(NumberIn[2]), .in1(NumberIn[1]), .in2(NumberIn[0]), .in3(1'b0), .out(multiplexer_2_out[2]),
    .sel(ShiftAmountIn));
  Multiplexer #(.enable("false"), .select(2)) multiplexer_5 (
    .in0(NumberIn[0]), .in1(NumberIn[1]), .in2(NumberIn[2]), .in3(RightFill), .out(multiplexer_5_out[0]),
    .sel(ShiftAmountIn));
  Multiplexer #(.enable("false"), .select(2)) multiplexer_6 (
    .in0(NumberIn[1]), .in1(NumberIn[2]), .in2(RightFill), .in3(RightFill), .out(multiplexer_5_out[1]),
    .sel(ShiftAmountIn));
  Multiplexer #(.enable("false"), .select(2)) multiplexer_7 (
    .in0(NumberIn[2]), .in1(RightFill), .in2(RightFill), .in3(RightFill), .out(multiplexer_5_out[2]),
    .sel(ShiftAmountIn));
  Multiplexer #(.enable("false"), .width(3)) multiplexer_8 (
    .in0(multiplexer_2_out), .in1(multiplexer_5_out), .out(ShiftedNumberOut), .sel(IsRightShiftIn));

  // Other names for the same wires on the sheet: IsArithmetic = IsArithmeticIn; IsRightShift = IsRightShiftIn;
  //   N0 = NumberIn[0]; Number[2:0] = NumberIn; N1 = NumberIn[1]; N2 = NumberIn[2]; ShiftAmount[1:0] = ShiftAmountIn;
  //   ShiftedNumber[2:0] = ShiftedNumberOut
endmodule
