// Logisim project FourBitParity.circ as structural Verilog: 3 circuits, main circuit Next_State
module Next_State (
  input  S2,
  input  S1,
  input  S0,
  input  BitInput,
  output S2_Output,
  output S1_Output,
  output S0_Output
);

  wire and_1_out, and_2_out, and_3_out, and_4_out, and_5_out, and_6_out, and_7_out, and_8_out, and_9_out,
       and_10_out, and_11_out, and_12_out, not_1_out, not_2_out, not_3_out, not_4_out, not_5_out, not_6_out,
       not_7_out, not_8_out, not_9_out, not_10_out, not_11_out;

  not not_1 (not_1_out, S2);
  not not_2 (not_2_out, S1);
  not not_3 (not_3_out, S0);
  not not_4 (not_4_out, BitInput);
  not not_5 (not_5_out, S2);
  not not_6 (not_6_out, S0);
  not not_7 (not_7_out, BitInput);
  not not_8 (not_8_out, S2);
  not not_9 (not_9_out, S1);
  not not_10 (not_10_out, S0);
  not not_11 (not_11_out, BitInput);
  and and_1 (and_1_out, S2, not_6_out, BitInput);
  and and_2 (and_2_out, not_9_out, S0, BitInput);
  and and_3 (and_3_out, S1, not_7_out);
  and and_4 (and_4_out, not_5_out, S0, BitInput);
  and and_5 (and_5_out, not_8_out, not_9_out, BitInput);
  and and_6 (and_6_out, not_8_out, not_9_out, S0);
  and and_7 (and_7_out, not_8_out, S1, not_11_out);
  and and_8 (and_8_out, S1, not_10_out, BitInput);
  and and_9 (and_9_out, S0, not_4_out);
  and and_10 (and_10_out, not_1_out, not_2_out, not_4_out);
  and and_11 (and_11_out, S1, not_3_out, BitInput);
  and and_12 (and_12_out, S2, not_3_out, BitInput);
  or or_1 (S2_Output, and_3_out, and_4_out, and_1_out);
  or or_2 (S1_Output, and_5_out, and_6_out, and_2_out, and_7_out, and_8_out);
  or or_3 (S0_Output, and_9_out, and_10_out, and_11_out, and_12_out);

  // Other names for the same wires on the sheet: S0_Next = S0_Output; S1_Next = S1_Output; S2_Next = S2_Output
endmodule

module FinalOutput (
  input  S2,
  input  S1,
  input  S0,
  output FinalOut
);

  wire not_1_out;

  not not_1 (not_1_out, S1);
  and and_1 (FinalOut, S2, not_1_out, S0);
endmodule

module implementation (
  input  EnableIn,
  input  InputBitIn,
  input  ClkIn,
  output IsEvenOut
);

  wire [2:0] next_state_1_s2_output, register_1_q;

  Next_State next_state_1 (
    .S2(register_1_q[0]), .S1(register_1_q[1]), .S0(register_1_q[2]), .BitInput(InputBitIn),
    .S2_Output(next_state_1_s2_output[0]), .S1_Output(next_state_1_s2_output[1]),
    .S0_Output(next_state_1_s2_output[2]));
  Register #(.width(3)) register_1 (
    .D(next_state_1_s2_output), .en(EnableIn), .clk(ClkIn), .Q(register_1_q));  // open: clr
  FinalOutput finaloutput_1 (.S2(register_1_q[2]), .S1(register_1_q[1]), .S0(register_1_q[0]), .FinalOut(IsEvenOut));

  // Other names for the same wires on the sheet: Clk = ClkIn; Enable = EnableIn; FinalOut = IsEvenOut;
  //   InputBit = InputBitIn
endmodule
