// Logisim project UpDownCounter.circ as structural Verilog: 2 circuits, main circuit implementation
module implementation (
  input  EnableIn,
  input  CountUpIn,
  input  CountDownIn,
  input  clkIn,
  output [2:0] Count
);

  wire [2:0] updown_circ_1_out_4;

  UpDown_circ updown_circ_1 (.in_1(Count), .in_2(CountUpIn), .in_3(CountDownIn), .out_4(updown_circ_1_out_4));
  Register #(.width(3)) register_1 (.D(updown_circ_1_out_4), .en(EnableIn), .clk(clkIn), .Q(Count));  // open: clr

  // Other names for the same wires on the sheet: clk = clkIn; CountDown = CountDownIn; CountOut[2:0] = Count;
  //   CountUp = CountUpIn; Enable = EnableIn
endmodule

module UpDown_circ (
  input  [2:0] in_1,
  input  in_2,
  input  in_3,
  output [2:0] out_4
);

  wire [0:0] adder_1_cout, subtractor_1_bout;
  wire [2:0] adder_1_out, adder_2_out, subtractor_1_out, subtractor_2_out;

  Subtractor #(.width(3)) subtractor_1 (
    .a(in_1), .b(3'b001), .out(subtractor_1_out), .bout(subtractor_1_bout[0]));  // open: bin
  Adder #(.width(3)) adder_1 (.a(in_1), .b(3'b001), .out(adder_1_out), .cout(adder_1_cout[0]));  // open: cin
  Adder #(.width(3)) adder_2 (
    .a(subtractor_1_out), .b({2'b00, subtractor_1_bout[0]}), .out(adder_2_out));  // open: cin, cout
  Subtractor #(.width(3)) subtractor_2 (
    .a(adder_1_out), .b({2'b00, adder_1_cout[0]}), .out(subtractor_2_out));  // open: bin, bout
  Multiplexer #(.enable("false"), .select(2), .width(3)) multiplexer_1 (
    .in0(in_1), .in1(adder_2_out), .in2(subtractor_2_out), .out(out_4), .sel({in_2, in_3}));  // open: in3

  // Other names for the same wires on the sheet: InputDown = in_3; InputUp = in_2; Bits[2:0] = in_1;
  //   CountOut[2:0] = out_4
endmodule
