// Logisim project Vending.circ as structural Verilog: 3 circuits, main circuit nextState
module nextState (
  input  S2,
  input  S1,
  input  S0,
  input  QuarterReceieved,
  input  DimeReceieved,
  input  NickelReceieved,
  output S2_Next,
  output S1_Next,
  output S0_Next
);

  wire and_1_out, and_2_out, and_3_out, and_4_out, and_5_out, and_6_out, and_7_out, and_8_out, and_9_out,
       and_10_out, and_11_out, and_12_out, and_13_out, and_14_out, and_15_out, and_16_out, and_17_out,
       and_18_out, and_19_out, and_20_out, and_21_out, and_22_out, and_23_out, and_24_out, and_25_out,
       and_26_out, and_27_out, and_28_out, and_29_out, and_30_out, and_31_out, and_32_out, and_33_out,
       and_34_out, and_35_out, and_36_out, not_1_out, not_2_out, not_3_out, not_4_out, not_5_out, not_6_out,
       not_7_out, not_8_out, not_9_out, not_10_out, not_11_out, not_12_out, not_13_out, not_14_out,
       not_15_out;

  not not_1 (not_1_out, S2);
  not not_2 (not_2_out, S1);
  not not_3 (not_3_out, S0);
  not not_4 (not_4_out, QuarterReceieved);
  not not_5 (not_5_out, DimeReceieved);
  not not_6 (not_6_out, NickelReceieved);
  and and_1 (and_1_out, not_4_out, not_5_out);
  and and_2 (and_2_out, not_5_out, not_6_out);
  and and_3 (and_3_out, not_4_out, not_5_out);
  and and_4 (and_4_out, S2, not_3_out, DimeReceieved);
  and and_5 (and_5_out, S2, not_4_out, QuarterReceieved, NickelReceieved);
  and and_6 (and_6_out, S2, not_2_out, not_4_out, not_5_out, NickelReceieved);
  and and_7 (and_7_out, S2, S0, not_4_out, not_5_out, not_6_out);
  and and_8 (and_8_out, not_1_out, not_2_out, not_3_out);
  and and_9 (and_9_out, QuarterReceieved, not_5_out, not_6_out);
  and and_10 (and_10_out, S2, not_2_out);
  and and_11 (and_11_out, not_4_out, not_5_out);
  and and_12 (and_12_out, not_5_out, not_6_out, S2, not_4_out, not_5_out);
  and and_13 (and_13_out, not_1_out, not_2_out);
  and and_14 (and_14_out, not_3_out, not_7_out);
  not not_7 (not_7_out, and_1_out);
  and and_15 (and_15_out, not_4_out, not_5_out);
  not not_8 (not_8_out, and_15_out);
  not not_9 (not_9_out, and_2_out);
  not not_10 (not_10_out, and_3_out);
  and and_16 (and_16_out, not_5_out, not_6_out);
  and and_17 (and_17_out, and_8_out, and_9_out);
  and and_18 (and_18_out, and_10_out, and_11_out);
  and and_19 (and_19_out, and_13_out, and_14_out);
  and and_20 (and_20_out, S1, not_3_out);
  and and_21 (and_21_out, not_5_out, not_6_out);
  not not_11 (not_11_out, and_21_out);
  and and_22 (and_22_out, not_5_out, not_6_out);
  not not_12 (not_12_out, and_22_out);
  and and_23 (and_23_out, not_4_out, not_5_out);
  not not_13 (not_13_out, and_23_out);
  and and_24 (and_24_out, not_1_out, not_2_out);
  and and_25 (and_25_out, not_3_out, not_8_out);
  and and_26 (and_26_out, not_2_out, not_3_out);
  and and_27 (and_27_out, not_9_out, not_10_out);
  not not_14 (not_14_out, and_16_out);
  and and_28 (and_28_out, not_5_out, not_6_out);
  not not_15 (not_15_out, and_28_out);
  and and_29 (and_29_out, and_20_out, not_11_out);
  and and_30 (and_30_out, not_3_out, not_12_out, not_13_out);
  and and_31 (and_31_out, and_24_out, and_25_out);
  and and_32 (and_32_out, not_1_out, not_3_out, not_4_out, not_5_out, not_14_out);
  and and_33 (and_33_out, not_1_out, S1, not_3_out, not_4_out, not_5_out);
  and and_34 (and_34_out, S2, S1, not_5_out, not_6_out, not_4_out, not_5_out);
  or or_1 (S0_Next, and_4_out, and_5_out, and_6_out, and_7_out, and_17_out);
  or or_2 (S2_Next, and_18_out, and_12_out, and_19_out, and_29_out, and_30_out);
  and and_35 (and_35_out, and_26_out, and_27_out);
  and and_36 (and_36_out, S2, not_2_out, S0, not_4_out, not_5_out, not_15_out);
  or or_3 (S1_Next, and_31_out, and_35_out, and_32_out, and_33_out, and_34_out, and_36_out);
endmodule

module finalOutput (
  input  S2,
  input  S1,
  input  S0,
  input  QuarterReceieved,
  input  DimeReceieved,
  input  NickelReceieved,
  output Give_Merchandis_Out,
  output Given_Dime_Out,
  output Given_Nickel_Out
);

  wire and_1_out, and_2_out, and_3_out, and_4_out, and_5_out, and_6_out, and_7_out, and_8_out, and_9_out,
       and_10_out, and_11_out, and_12_out, and_13_out, and_14_out, and_15_out, and_16_out, and_17_out,
       and_18_out, and_19_out, and_20_out, and_21_out, and_22_out, and_23_out, and_24_out, not_1_out,
       not_2_out, not_3_out, not_4_out, not_5_out, not_6_out, not_7_out, not_8_out, not_9_out, not_10_out;

  not not_1 (not_1_out, S1);
  not not_2 (not_2_out, QuarterReceieved);
  not not_3 (not_3_out, DimeReceieved);
  not not_4 (not_4_out, NickelReceieved);
  and and_1 (and_1_out, not_2_out, not_3_out);
  and and_2 (and_2_out, not_2_out, not_3_out);
  not not_5 (not_5_out, and_2_out);
  and and_3 (and_3_out, S0, QuarterReceieved);
  and and_4 (and_4_out, not_2_out, not_3_out);
  not not_6 (not_6_out, and_4_out);
  and and_5 (and_5_out, not_2_out, not_3_out);
  not not_7 (not_7_out, and_1_out);
  and and_6 (and_6_out, not_3_out, not_4_out);
  and and_7 (and_7_out, not_3_out, not_4_out);
  and and_8 (and_8_out, not_2_out, not_3_out);
  not not_8 (not_8_out, and_8_out);
  and and_9 (and_9_out, S1, S0, DimeReceieved);
  and and_10 (and_10_out, S1, S0, QuarterReceieved);
  and and_11 (and_11_out, not_3_out, not_4_out);
  and and_12 (and_12_out, S2, S1, QuarterReceieved, not_3_out, not_4_out);
  and and_13 (and_13_out, not_3_out, not_4_out);
  and and_14 (and_14_out, S0, not_6_out);
  and and_15 (and_15_out, S2, not_1_out, not_3_out, not_4_out, not_9_out);
  not not_9 (not_9_out, and_5_out);
  and and_16 (and_16_out, S0, not_7_out);
  and and_17 (and_17_out, S1, not_5_out);
  not not_10 (not_10_out, and_7_out);
  and and_18 (and_18_out, not_3_out, not_4_out);
  and and_19 (and_19_out, S2, not_8_out);
  and and_20 (and_20_out, and_3_out, and_11_out);
  and and_21 (and_21_out, and_13_out, and_14_out);
  and and_22 (and_22_out, and_6_out, and_17_out);
  and and_23 (and_23_out, S1, S0, not_10_out);
  and and_24 (and_24_out, and_18_out, and_19_out);
  or or_1 (Given_Nickel_Out, and_9_out, and_10_out, and_20_out, and_12_out);
  or or_2 (Given_Dime_Out, and_21_out, and_15_out);
  or or_3 (Give_Merchandis_Out, and_16_out, and_22_out, and_23_out, and_24_out);
endmodule

module implementation (
  input  EnableIn,
  input  QuarterReceivedIn,
  input  DimeReceivedIn,
  input  NickelReceivedIn,
  input  ClkIn,
  output Give_Merchandise_Out,
  output Give_Dime_Out,
  output Give_Nickel_Out
);

  wire [2:0] nextstate_1_s0_next, register_1_q;

  nextState nextstate_1 (
    .S2(register_1_q[2]), .S1(register_1_q[1]), .S0(register_1_q[0]), .QuarterReceieved(QuarterReceivedIn),
    .DimeReceieved(DimeReceivedIn), .NickelReceieved(NickelReceivedIn), .S2_Next(nextstate_1_s0_next[2]),
    .S1_Next(nextstate_1_s0_next[1]), .S0_Next(nextstate_1_s0_next[0]));
  Register #(.width(3)) register_1 (
    .D(nextstate_1_s0_next), .en(EnableIn), .clk(ClkIn), .Q(register_1_q));  // open: clr
  finalOutput finaloutput_1 (
    .S2(register_1_q[2]), .S1(register_1_q[1]), .S0(register_1_q[0]), .QuarterReceieved(QuarterReceivedIn),
    .DimeReceieved(DimeReceivedIn), .NickelReceieved(NickelReceivedIn),
    .Give_Merchandis_Out(Give_Merchandise_Out), .Given_Dime_Out(Give_Dime_Out),
    .Given_Nickel_Out(Give_Nickel_Out));

  // Other names for the same wires on the sheet: Clk = ClkIn; DimeReceieved = DimeReceivedIn; Enable = EnableIn;
  //   Give_Dime = Give_Dime_Out; Give_Merchandise = Give_Merchandise_Out; Give_Nickel = Give_Nickel_Out;
  //   NickelReceieved = NickelReceivedIn; QuarterReceieved = QuarterReceivedIn
endmodule
