// Logisim project CPU.circ as structural Verilog: 5 circuits, main circuit implementation
module implementation (
  input  [15:0] Instruction_In,
  input  ClkIn,
  output [4:0] Instruction_Address_Out,
  output [3:0] Reg0_Out,
  output [3:0] Reg1_Out,
  output [3:0] Reg2_Out,
  output [3:0] Reg3_Out,
  output [3:0] Reg4_Out,
  output [3:0] Reg5_Out,
  output [3:0] Reg6_Out,
  output [3:0] Reg7_Out,
  output [3:0] Reg8_Out,
  output [3:0] Reg9_Out,
  output [3:0] Reg10_Out,
  output [3:0] Reg11_Out,
  output [3:0] Reg12_Out,
  output [3:0] Reg13_Out,
  output [3:0] Reg14_Out,
  output [3:0] Reg15_Out
);

  wire Immediate, Reg_Write, Stop;
  wire [3:0] A_Value, ALU_Output, B_Value, multiplexer_1_out;

  Multiplexer #(.enable("false"), .width(4)) multiplexer_1 (
    .in0(B_Value), .in1(Instruction_In[3:0]), .out(multiplexer_1_out), .sel(Immediate));
  InstructionDecoder instructiondecoder_1 (
    .Opcode(Instruction_In[15:12]), .out_2(Reg_Write), .out_3(Stop), .out_4(Immediate));
  ALU alu_1 (.in_1(Instruction_In[15:12]), .A_Value(A_Value), .B_Value(multiplexer_1_out), .ALUOutput(ALU_Output));
  RegFile regfile_1 (
    .A_Sel_In(Instruction_In[7:4]), .B_Sel_In(Instruction_In[3:0]), .C_Sel_In(Instruction_In[11:8]),
    .Data_In(ALU_Output), .Reg_Write_In(Reg_Write), .clk_in(ClkIn), .A_Out(A_Value), .B_Out(B_Value),
    .Reg0_Out(Reg0_Out), .Reg1_Out(Reg1_Out), .Reg2_Out(Reg2_Out), .Reg3_Out(Reg3_Out), .Reg4_Out(Reg4_Out),
    .Reg5_Out(Reg5_Out), .Reg6_Out(Reg6_Out), .Reg7_Out(Reg7_Out), .Reg8_Out(Reg8_Out), .Reg9_Out(Reg9_Out),
    .Reg10_Out(Reg10_Out), .Reg11_Out(Reg11_Out), .Reg12_Out(Reg12_Out), .Reg13_Out(Reg13_Out),
    .Reg14_Out(Reg14_Out), .Reg15_Out(Reg15_Out));
  PC pc_1 (.ClkIn(ClkIn), .Stop(Stop), .Instruction(Instruction_Address_Out));

  // Other names for the same wires on the sheet: Clk = ClkIn; B[3:0] = Instruction_In[3:0];
  //   Imm[3:0] = Instruction_In[3:0]; Instruction[15:0] = Instruction_In; A[3:0] = Instruction_In[7:4];
  //   C[3:0] = Instruction_In[11:8]; Opcode[3:0] = Instruction_In[15:12];
  //   Instruction_Address[4:0] = Instruction_Address_Out; Reg0[3:0] = Reg0_Out; Reg1[3:0] = Reg1_Out;
  //   Reg2[3:0] = Reg2_Out; Reg3[3:0] = Reg3_Out; Reg4[3:0] = Reg4_Out; Reg5[3:0] = Reg5_Out; Reg6[3:0] = Reg6_Out;
  //   Reg7[3:0] = Reg7_Out; Reg8[3:0] = Reg8_Out; Reg9[3:0] = Reg9_Out; Reg10[3:0] = Reg10_Out;
  //   Reg11[3:0] = Reg11_Out; Reg12[3:0] = Reg12_Out; Reg13[3:0] = Reg13_Out; Reg14[3:0] = Reg14_Out;
  //   Reg15[3:0] = Reg15_Out
endmodule

module RegFile (
  input  [3:0] A_Sel_In,
  input  [3:0] B_Sel_In,
  input  [3:0] C_Sel_In,
  input  [3:0] Data_In,
  input  Reg_Write_In,
  input  clk_in,
  output [3:0] A_Out,
  output [3:0] B_Out,
  output [3:0] Reg0_Out,
  output [3:0] Reg1_Out,
  output [3:0] Reg2_Out,
  output [3:0] Reg3_Out,
  output [3:0] Reg4_Out,
  output [3:0] Reg5_Out,
  output [3:0] Reg6_Out,
  output [3:0] Reg7_Out,
  output [3:0] Reg8_Out,
  output [3:0] Reg9_Out,
  output [3:0] Reg10_Out,
  output [3:0] Reg11_Out,
  output [3:0] Reg12_Out,
  output [3:0] Reg13_Out,
  output [3:0] Reg14_Out,
  output [3:0] Reg15_Out
);

  wire Reg_Write0, Reg_Write1, Reg_Write2, Reg_Write3, Reg_Write4, Reg_Write5, Reg_Write6, Reg_Write7,
       Reg_Write8, Reg_Write9, Reg_Write10, Reg_Write11, Reg_Write12, Reg_Write13, Reg_Write14, Reg_Write15;

  Demultiplexer #(.enable("false"), .select(4)) demultiplexer_1 (
    .out0(Reg_Write0), .out1(Reg_Write1), .out2(Reg_Write2), .out3(Reg_Write3), .out4(Reg_Write4),
    .out5(Reg_Write5), .out6(Reg_Write6), .out7(Reg_Write7), .out8(Reg_Write8), .out9(Reg_Write9),
    .out10(Reg_Write10), .out11(Reg_Write11), .out12(Reg_Write12), .out13(Reg_Write13), .out14(Reg_Write14),
    .out15(Reg_Write15), .in(Reg_Write_In), .sel(C_Sel_In));
  Register #(.width(4)) register_1 (.D(Data_In), .en(Reg_Write0), .clk(clk_in), .Q(Reg0_Out));  // open: clr
  Register #(.width(4)) register_2 (.D(Data_In), .en(Reg_Write4), .clk(clk_in), .Q(Reg4_Out));  // open: clr
  Register #(.width(4)) register_3 (.D(Data_In), .en(Reg_Write8), .clk(clk_in), .Q(Reg8_Out));  // open: clr
  Register #(.width(4)) register_4 (.D(Data_In), .en(Reg_Write12), .clk(clk_in), .Q(Reg12_Out));  // open: clr
  Register #(.width(4)) register_5 (.D(Data_In), .en(Reg_Write1), .clk(clk_in), .Q(Reg1_Out));  // open: clr
  Register #(.width(4)) register_6 (.D(Data_In), .en(Reg_Write5), .clk(clk_in), .Q(Reg5_Out));  // open: clr
  Register #(.width(4)) register_7 (.D(Data_In), .en(Reg_Write9), .clk(clk_in), .Q(Reg9_Out));  // open: clr
  Register #(.width(4)) register_8 (.D(Data_In), .en(Reg_Write13), .clk(clk_in), .Q(Reg13_Out));  // open: clr
  Register #(.width(4)) register_9 (.D(Data_In), .en(Reg_Write2), .clk(clk_in), .Q(Reg2_Out));  // open: clr
  Register #(.width(4)) register_10 (.D(Data_In), .en(Reg_Write6), .clk(clk_in), .Q(Reg6_Out));  // open: clr
  Register #(.width(4)) register_11 (.D(Data_In), .en(Reg_Write10), .clk(clk_in), .Q(Reg10_Out));  // open: clr
  Register #(.width(4)) register_12 (.D(Data_In), .en(Reg_Write14), .clk(clk_in), .Q(Reg14_Out));  // open: clr
  Register #(.width(4)) register_13 (.D(Data_In), .en(Reg_Write3), .clk(clk_in), .Q(Reg3_Out));  // open: clr
  Register #(.width(4)) register_14 (.D(Data_In), .en(Reg_Write7), .clk(clk_in), .Q(Reg7_Out));  // open: clr
  Register #(.width(4)) register_15 (.D(Data_In), .en(Reg_Write11), .clk(clk_in), .Q(Reg11_Out));  // open: clr
  Register #(.width(4)) register_16 (.D(Data_In), .en(Reg_Write15), .clk(clk_in), .Q(Reg15_Out));  // open: clr
  Multiplexer #(.enable("false"), .select(4), .width(4)) multiplexer_1 (
    .in0(Reg0_Out), .in1(Reg1_Out), .in2(Reg2_Out), .in3(Reg3_Out), .in4(Reg4_Out), .in5(Reg5_Out),
    .in6(Reg6_Out), .in7(Reg7_Out), .in8(Reg8_Out), .in9(Reg9_Out), .in10(Reg10_Out), .in11(Reg11_Out),
    .in12(Reg12_Out), .in13(Reg13_Out), .in14(Reg14_Out), .in15(Reg15_Out), .out(A_Out), .sel(A_Sel_In));
  Multiplexer #(.enable("false"), .select(4), .width(4)) multiplexer_2 (
    .in0(Reg0_Out), .in1(Reg1_Out), .in2(Reg2_Out), .in3(Reg3_Out), .in4(Reg4_Out), .in5(Reg5_Out),
    .in6(Reg6_Out), .in7(Reg7_Out), .in8(Reg8_Out), .in9(Reg9_Out), .in10(Reg10_Out), .in11(Reg11_Out),
    .in12(Reg12_Out), .in13(Reg13_Out), .in14(Reg14_Out), .in15(Reg15_Out), .out(B_Out), .sel(B_Sel_In));

  // Other names for the same wires on the sheet: A[3:0] = A_Out; A_Sel[3:0] = A_Sel_In; B[3:0] = B_Out;
  //   B_Sel[3:0] = B_Sel_In; C_Sel[3:0] = C_Sel_In; clk = clk_in; Data[3:0] = Data_In; Reg0[3:0] = Reg0_Out;
  //   Reg1[3:0] = Reg1_Out; Reg2[3:0] = Reg2_Out; Reg3[3:0] = Reg3_Out; Reg4[3:0] = Reg4_Out; Reg5[3:0] = Reg5_Out;
  //   Reg6[3:0] = Reg6_Out; Reg7[3:0] = Reg7_Out; Reg8[3:0] = Reg8_Out; Reg9[3:0] = Reg9_Out; Reg10[3:0] = Reg10_Out;
  //   Reg11[3:0] = Reg11_Out; Reg12[3:0] = Reg12_Out; Reg13[3:0] = Reg13_Out; Reg14[3:0] = Reg14_Out;
  //   Reg15[3:0] = Reg15_Out; Reg_Write = Reg_Write_In
endmodule

module InstructionDecoder (
  input  [3:0] Opcode,
  output out_2,
  output out_3,
  output out_4
);

  Multiplexer #(.enable("false"), .select(4)) multiplexer_1 (
    .in0(1'b0), .in1(1'b0), .in2(1'b1), .in3(1'b1), .in4(1'b1), .in5(1'b1), .in6(1'b1), .in7(1'b1),
    .in8(1'b1), .in9(1'b1), .in10(1'b1), .in11(1'b1), .in12(1'b1), .in13(1'b1), .in14(1'b1), .in15(1'b1),
    .out(out_2), .sel(Opcode));
  Multiplexer #(.enable("false"), .select(4)) multiplexer_2 (
    .in0(1'b1), .in1(1'b0), .in2(1'b0), .in3(1'b0), .in4(1'b0), .in5(1'b0), .in6(1'b0), .in7(1'b0),
    .in8(1'b0), .in9(1'b0), .in10(1'b0), .in11(1'b0), .in12(1'b0), .in13(1'b0), .in14(1'b0), .in15(1'b0),
    .out(out_3), .sel(Opcode));
  Multiplexer #(.enable("false"), .select(4)) multiplexer_3 (
    .in0(1'b0), .in1(1'b0), .in2(1'b1), .in3(1'b0), .in4(1'b0), .in5(1'b1), .in6(1'b0), .in7(1'b1),
    .in8(1'b0), .in9(1'b1), .in10(1'b0), .in11(1'b0), .in12(1'b0), .in13(1'b1), .in14(1'b0), .in15(1'b1),
    .out(out_4), .sel(Opcode));

  // Other names for the same wires on the sheet: Immediate = out_4; Reg_Write = out_2; Stop = out_3
endmodule

module ALU (
  input  [3:0] in_1,
  input  [3:0] A_Value,
  input  [3:0] B_Value,
  output [3:0] ALUOutput
);

  wire [3:0] adder_1_out, and_1_out, negator_1_out, not_1_out, or_1_out, subtractor_1_out, xor_1_out;

  assign and_1_out = B_Value & A_Value;  // AND_Gate and_1, 4 bits wide
  assign or_1_out = B_Value | A_Value;  // OR_Gate or_1, 4 bits wide
  assign xor_1_out = B_Value ^ A_Value;  // XOR_Gate xor_1, 4 bits wide
  assign not_1_out = ~A_Value;  // NOT_Gate not_1, 4 bits wide
  Negator #(.width(4)) negator_1 (.in(A_Value), .out(negator_1_out));
  Adder #(.width(4)) adder_1 (.a(A_Value), .b(B_Value), .out(adder_1_out));  // open: cin, cout
  Subtractor #(.width(4)) subtractor_1 (.a(A_Value), .b(B_Value), .out(subtractor_1_out));  // open: bin, bout
  Multiplexer #(.enable("false"), .select(4), .width(4)) multiplexer_1 (
    .in0(4'b0000), .in1(4'b0000), .in2(B_Value), .in3(A_Value), .in4(and_1_out), .in5(and_1_out),
    .in6(or_1_out), .in7(or_1_out), .in8(xor_1_out), .in9(xor_1_out), .in10(not_1_out), .in11(negator_1_out),
    .in12(adder_1_out), .in13(adder_1_out), .in14(subtractor_1_out), .in15(subtractor_1_out),
    .out(ALUOutput), .sel(in_1));

  // Other names for the same wires on the sheet: A[3:0] = A_Value; B[3:0] = B_Value; Control[3:0] = in_1
endmodule

module PC (
  input  ClkIn,
  input  Stop,
  output [4:0] Instruction
);

  wire not_1_out;
  wire [4:0] adder_1_out;

  not not_1 (not_1_out, Stop);
  Register #(.width(5)) register_1 (.D(adder_1_out), .en(not_1_out), .clk(ClkIn), .Q(Instruction));  // open: clr
  Adder #(.width(5)) adder_1 (.a(Instruction), .b(5'b00001), .out(adder_1_out));  // open: cin, cout

  // Other names for the same wires on the sheet: Clk = ClkIn; Instruction_Address[4:0] = Instruction
endmodule
