// Logisim project Cache.circ as structural Verilog: 6 circuits, main circuit implementation
module implementation (
  input  [9:0] CpuAddressIn,
  input  CpuReadIn,
  input  CpuWriteIn,
  input  [7:0] CpuWriteValueIn,
  input  [31:0] LineFromMemIn,
  input  ClkIn,
  output ReadyOut,
  output DidContainOut,
  output [7:0] ByteReadOut,
  output [7:0] MemAddressOut,
  output MemReadOut,
  output MemWriteOut,
  output [31:0] Line2MemOut
);

  wire control_1_age0out, control_1_age1out, control_1_byte0out, control_1_byte1out,
       control_1_initializationout, control_1_line0out, control_1_line1out, newContain, set1_1_contain,
       set1_1_dirty;
  wire [6:0] Tag;
  wire [9:0] CpuAddressOut;

  set1 set1_1 (
    .lineFromMem(LineFromMemIn), .CpuAddressOut(CpuAddressOut), .CpuWriteValue(CpuWriteValueIn),
    .initialize(control_1_initializationout), .age0(control_1_age0out), .age1(control_1_age1out),
    .line0(control_1_line0out), .line1(control_1_line1out), .byte0(control_1_byte0out),
    .byte1(control_1_byte1out), .clk(ClkIn), .sets(CpuAddressOut[2]), .Tag(Tag), .Dirty(set1_1_dirty),
    .Line2Mem(Line2MemOut), .ByteRead(ByteReadOut), .Contain(set1_1_contain));
  Register #(.width(1)) register_1 (.D(set1_1_contain), .en(newContain), .clk(ClkIn), .Q(DidContainOut));  // open: clr
  control control_1 (
    .CpuAddress(CpuAddressIn), .write(CpuWriteIn), .read(CpuReadIn), .contain(set1_1_contain),
    .dirty(set1_1_dirty), .clkIn(ClkIn), .CpuAddressOut(CpuAddressOut), .readyOut(ReadyOut),
    .memReadOut(MemReadOut), .memWriteOut(MemWriteOut), .initializationOut(control_1_initializationout),
    .ContainOut(newContain), .age0Out(control_1_age0out), .age1Out(control_1_age1out),
    .line0Out(control_1_line0out), .line1Out(control_1_line1out), .byte0Out(control_1_byte0out),
    .byte1Out(control_1_byte1out));
  Multiplexer #(.enable("false"), .width(8)) multiplexer_1 (
    .in0(CpuAddressOut[9:2]), .in1({Tag, CpuAddressOut[2]}), .out(MemAddressOut), .sel(MemWriteOut));

  // Other names for the same wires on the sheet: tag_t[6:0] = CpuAddressOut[9:3]; sets = CpuAddressOut[2];
  //   clk = ClkIn; CpuAddress[9:0] = CpuAddressIn; offSet[1:0] = CpuAddressOut[1:0]; CpuRead = CpuReadIn;
  //   CpuWrite = CpuWriteIn; CpuWriteValue[7:0] = CpuWriteValueIn; DidContain = DidContainOut;
  //   LineFromMem[31:0] = LineFromMemIn; MemAddress[7:0] = MemAddressOut; MemRead = MemReadOut;
  //   MemWrite = MemWriteOut; Ready = ReadyOut; ByteRead[7:0] = ByteReadOut; SelectedSetByteRead[7:0] = ByteReadOut;
  //   Line2Mem[31:0] = Line2MemOut; SelectedSetLine2Mem[31:0] = Line2MemOut

  // Notes on the sheet:
  //   Yihe Liu 918447001
  //   Yiming Peng 918343422
endmodule

module fsm (
  input  S0,
  input  S1,
  input  S2,
  input  read,
  input  write,
  input  contain,
  input  dirty,
  output ready,
  output memRead,
  output Out2,
  output memWrite,
  output initialization,
  output OneBlock,
  output OneByte,
  output Out0,
  output newContain,
  output newAge,
  output Out1
);

  wire and_8_out, and_9_out, and_10_out, and_11_out, and_12_out, and_13_out, and_14_out, and_15_out,
       and_16_out, and_17_out, and_18_out, and_19_out, and_20_out, and_21_out, and_22_out, and_23_out,
       and_24_out, and_25_out, and_26_out, and_27_out, and_28_out, and_29_out, and_30_out, not_1_out,
       not_2_out, not_3_out, not_4_out, not_5_out, not_6_out, not_7_out, not_8_out, not_9_out, not_10_out,
       not_11_out, not_12_out, not_13_out, not_14_out, not_15_out, not_16_out, not_17_out, not_18_out,
       not_19_out, not_20_out, not_21_out, not_22_out, not_23_out, not_24_out, not_25_out, not_26_out,
       not_27_out, not_28_out, not_29_out, not_30_out, not_31_out, not_32_out, not_33_out, not_34_out,
       not_35_out, not_36_out, not_37_out, not_38_out, not_39_out, not_40_out, not_41_out, not_42_out;

  not not_1 (not_1_out, S2);
  not not_2 (not_2_out, S1);
  not not_3 (not_3_out, S1);
  not not_4 (not_4_out, S0);
  not not_5 (not_5_out, S2);
  not not_6 (not_6_out, S2);
  not not_7 (not_7_out, S1);
  not not_8 (not_8_out, S0);
  not not_9 (not_9_out, S1);
  not not_10 (not_10_out, S0);
  not not_11 (not_11_out, S0);
  not not_12 (not_12_out, S2);
  not not_13 (not_13_out, S0);
  not not_14 (not_14_out, S2);
  not not_15 (not_15_out, S1);
  not not_16 (not_16_out, S0);
  not not_17 (not_17_out, S1);
  not not_18 (not_18_out, S1);
  not not_19 (not_19_out, read);
  not not_20 (not_20_out, S2);
  not not_21 (not_21_out, S1);
  not not_22 (not_22_out, S0);
  not not_23 (not_23_out, S2);
  not not_24 (not_24_out, S0);
  not not_25 (not_25_out, contain);
  and and_1 (ready, not_1_out, not_2_out, S0);
  and and_2 (memRead, S2, not_3_out, not_4_out);
  and and_3 (memWrite, not_5_out, S1, S0);
  and and_4 (initialization, not_6_out, not_7_out, not_8_out);
  and and_5 (OneBlock, S2, not_9_out, not_10_out);
  and and_6 (OneByte, S2, S1, not_11_out);
  and and_7 (newContain, not_12_out, S1, not_13_out);
  and and_8 (and_8_out, not_14_out, not_15_out, not_16_out);
  and and_9 (and_9_out, S2, not_17_out, S0);
  and and_10 (and_10_out, not_18_out, S0);
  and and_11 (and_11_out, not_19_out, write);
  and and_12 (and_12_out, not_20_out, not_21_out);
  and and_13 (and_13_out, S0, read);
  and and_14 (and_14_out, S2, not_22_out);
  and and_15 (and_15_out, read, write);
  and and_16 (and_16_out, and_10_out, and_11_out);
  and and_17 (and_17_out, and_12_out, and_13_out);
  and and_18 (and_18_out, and_14_out, and_15_out);
  and and_19 (and_19_out, not_23_out, S1, not_24_out, not_25_out, dirty);
  or or_1 (newAge, and_8_out, and_9_out);
  or or_2 (Out1, and_16_out, and_17_out, and_18_out, and_19_out);
  not not_26 (not_26_out, S2);
  not not_27 (not_27_out, dirty);
  not not_28 (not_28_out, S2);
  not not_29 (not_29_out, S1);
  not not_30 (not_30_out, S0);
  not not_31 (not_31_out, S1);
  not not_32 (not_32_out, read);
  not not_33 (not_33_out, S1);
  not not_34 (not_34_out, S0);
  not not_35 (not_35_out, S0);
  not not_36 (not_36_out, S0);
  not not_37 (not_37_out, S1);
  not not_38 (not_38_out, read);
  not not_39 (not_39_out, write);
  not not_40 (not_40_out, S0);
  and and_20 (and_20_out, not_33_out, not_34_out);
  and and_21 (and_21_out, not_35_out, dirty);
  and and_22 (and_22_out, not_36_out, contain);
  and and_23 (and_23_out, not_37_out, not_38_out, not_39_out);
  and and_24 (and_24_out, S2, not_40_out);
  not not_41 (not_41_out, S1);
  not not_42 (not_42_out, write);
  and and_25 (and_25_out, not_26_out, S1, not_27_out);
  and and_26 (and_26_out, not_28_out, S1, contain);
  and and_27 (and_27_out, S2, not_29_out, not_30_out);
  and and_28 (and_28_out, S2, not_31_out, not_32_out);
  and and_29 (and_29_out, S1, S0);
  and and_30 (and_30_out, S2, not_41_out, not_42_out);
  or or_3 (Out2, and_25_out, and_26_out, and_27_out, and_28_out, and_29_out);
  or or_4 (Out0, and_20_out, and_21_out, and_22_out, and_23_out, and_24_out, and_30_out);
endmodule

module Set (
  input  [9:0] CpuAddressOut,
  input  Initialize,
  input  Ages,
  input  [7:0] CpuWriteValueIn,
  input  [31:0] LineFromMemIn,
  input  Ways,
  input  Bytes,
  input  ClkIn,
  output [6:0] Tag,
  output Dirty,
  output [31:0] Line2Mem,
  output [7:0] ByteRead,
  output DidContain
);

  wire Byte0, Byte1, Byte2, Contain0, Contain1, Contain2, Dirty0, Dirty1, Dirty2, Valid0, Valid1, Valid2,
       Way0, Way1, Way2;
  wire [1:0] Age0, Age1, Age2, multiplexer_4_out, NewAge, SelectOut;
  wire [2:0] comparator_1_eq;
  wire [6:0] Tag0, Tag1, Tag2;
  wire [7:0] ByteRead0, ByteRead1, ByteRead2;
  wire [31:0] Line2Mem0, Line2Mem1, Line2Mem2;

  Demultiplexer #(.enable("false"), .select(2)) demultiplexer_1 (
    .out0(Way0), .out1(Way1), .out2(Way2), .in(Ways), .sel(SelectOut));  // open: out3
  Demultiplexer #(.enable("false"), .select(2)) demultiplexer_2 (
    .out0(Byte0), .out1(Byte1), .out2(Byte2), .in(Bytes), .sel(SelectOut));  // open: out3
  Way way_1 (
    .CpuAddress(CpuAddressOut), .Initialize(Initialize), .Ages(Ages), .CpuWriteValueIn(CpuWriteValueIn),
    .LineFromMemIn(LineFromMemIn), .Ways(Way0), .Bytes(Byte0), .InitialAge(2'b00), .NewAge(NewAge),
    .clk(ClkIn), .UpdatedAge(Age0), .UpdatedTag(Tag0), .UpdatedDirty(Dirty0), .UpdatedValid(Valid0),
    .DidContain(Contain0), .Line2Mem(Line2Mem0), .ByteRead(ByteRead0));
  Way way_2 (
    .CpuAddress(CpuAddressOut), .Initialize(Initialize), .Ages(Ages), .CpuWriteValueIn(CpuWriteValueIn),
    .LineFromMemIn(LineFromMemIn), .Ways(Way1), .Bytes(Byte1), .InitialAge(2'b01), .NewAge(NewAge),
    .clk(ClkIn), .UpdatedAge(Age1), .UpdatedTag(Tag1), .UpdatedDirty(Dirty1), .UpdatedValid(Valid1),
    .DidContain(Contain1), .Line2Mem(Line2Mem1), .ByteRead(ByteRead1));
  Way way_3 (
    .CpuAddress(CpuAddressOut), .Initialize(Initialize), .Ages(Ages), .CpuWriteValueIn(CpuWriteValueIn),
    .LineFromMemIn(LineFromMemIn), .Ways(Way2), .Bytes(Byte2), .InitialAge(2'b10), .NewAge(NewAge),
    .clk(ClkIn), .UpdatedAge(Age2), .UpdatedTag(Tag2), .UpdatedDirty(Dirty2), .UpdatedValid(Valid2),
    .DidContain(Contain2), .Line2Mem(Line2Mem2), .ByteRead(ByteRead2));
  Multiplexer #(.enable("false"), .select(2), .width(7)) multiplexer_1 (
    .in0(Tag0), .in1(Tag1), .in2(Tag2), .out(Tag), .sel(SelectOut));  // open: in3
  Multiplexer #(.enable("false"), .select(2)) multiplexer_2 (
    .in0(Dirty0), .in1(Dirty1), .in2(Dirty2), .out(Dirty), .sel(SelectOut));  // open: in3
  Comparator #(.mode("unsigned"), .width(2)) comparator_1 (
    .a(Age0), .b(2'b10), .eq(comparator_1_eq[0]));  // open: gt, lt
  Comparator #(.mode("unsigned"), .width(2)) comparator_2 (
    .a(Age1), .b(2'b10), .eq(comparator_1_eq[1]));  // open: gt, lt
  Comparator #(.mode("unsigned"), .width(2)) comparator_3 (
    .a(Age2), .b(2'b10), .eq(comparator_1_eq[2]));  // open: gt, lt
  Multiplexer #(.enable("false"), .select(2), .width(32)) multiplexer_3 (
    .in0(Line2Mem0), .in1(Line2Mem1), .in2(Line2Mem2), .out(Line2Mem), .sel(SelectOut));  // open: in3
  or or_1 (DidContain, Contain0, Contain1, Contain2);
  Multiplexer #(.enable("false"), .select(3), .width(2)) multiplexer_4 (
    .in1(2'b00), .in2(2'b01), .in4(2'b10), .out(multiplexer_4_out), .sel(comparator_1_eq));  // open: in0, in3, in5, in6, in7
  Multiplexer #(.enable("false"), .select(3), .width(2)) multiplexer_5 (
    .in0(multiplexer_4_out), .in1(2'b00), .in2(2'b01), .in4(2'b10), .out(SelectOut),
    .sel({Contain2, Contain1, Contain0}));  // open: in3, in5, in6, in7
  Multiplexer #(.enable("false"), .select(2), .width(2)) multiplexer_6 (
    .in0(Age0), .in1(Age1), .in2(Age2), .out(NewAge), .sel(SelectOut));  // open: in3
  Multiplexer #(.enable("false"), .select(2), .width(8)) multiplexer_7 (
    .in0(ByteRead0), .in1(ByteRead1), .in2(ByteRead2), .out(ByteRead), .sel(SelectOut));  // open: in3

  // Other names for the same wires on the sheet: Clk = ClkIn; CpuAddress[9:0] = CpuAddressOut;
  //   CpuWriteValue[7:0] = CpuWriteValueIn; LineFromMem[31:0] = LineFromMemIn
endmodule

module Way (
  input  [9:0] CpuAddress,
  input  Initialize,
  input  Ages,
  input  [7:0] CpuWriteValueIn,
  input  [31:0] LineFromMemIn,
  input  Ways,
  input  Bytes,
  input  [1:0] InitialAge,
  input  [1:0] NewAge,
  input  clk,
  output [1:0] UpdatedAge,
  output [6:0] UpdatedTag,
  output UpdatedDirty,
  output UpdatedValid,
  output DidContain,
  output [31:0] Line2Mem,
  output [7:0] ByteRead
);

  wire Byte0, Byte1, Byte2, Byte3, comparator_1_eq, comparator_2_eq, comparator_2_gt, not_1_out, or_1_out,
       or_2_out, or_3_out, or_4_out, or_5_out, or_6_out, or_7_out;
  wire [1:0] adder_1_out, multiplexer_3_out, multiplexer_4_out, multiplexer_8_out;
  wire [7:0] multiplexer_1_out, multiplexer_2_out, multiplexer_5_out, multiplexer_6_out;

  or or_1 (or_1_out, Ages, Initialize);
  Register #(.width(7)) register_1 (.D(CpuAddress[9:3]), .en(Ways), .clk(clk), .Q(UpdatedTag));  // open: clr
  or or_2 (or_2_out, Byte0, Ways);
  or or_3 (or_3_out, Byte2, Ways);
  Register #(.width(2)) register_2 (.D(multiplexer_8_out), .en(or_1_out), .clk(clk), .Q(UpdatedAge));  // open: clr
  Comparator #(.width(7)) comparator_1 (.a(UpdatedTag), .b(CpuAddress[9:3]), .eq(comparator_1_eq));  // open: gt, lt
  Multiplexer #(.enable("false"), .width(8)) multiplexer_1 (
    .in0(LineFromMemIn[7:0]), .in1(CpuWriteValueIn), .out(multiplexer_1_out), .sel(Bytes));
  Register register_3 (.D(multiplexer_2_out), .en(or_3_out), .clk(clk), .Q(Line2Mem[23:16]));  // open: clr
  Multiplexer #(.enable("false"), .width(8)) multiplexer_2 (
    .in0(LineFromMemIn[23:16]), .in1(CpuWriteValueIn), .out(multiplexer_2_out), .sel(Bytes));
  and and_1 (DidContain, comparator_1_eq, UpdatedValid);
  Register register_4 (.D(multiplexer_1_out), .en(or_2_out), .clk(clk), .Q(Line2Mem[7:0]));  // open: clr
  Adder #(.width(2)) adder_1 (.a(UpdatedAge), .b(2'b01), .out(adder_1_out));  // open: cin, cout
  not not_1 (not_1_out, Ways);
  or or_4 (or_4_out, not_1_out, Bytes);
  or or_5 (or_5_out, Bytes, Ways);
  Comparator #(.mode("unsigned"), .width(2)) comparator_2 (
    .a(UpdatedAge), .b(NewAge), .gt(comparator_2_gt), .eq(comparator_2_eq));  // open: lt
  Multiplexer #(.enable("false"), .width(2)) multiplexer_3 (
    .in0(adder_1_out), .in1(2'b00), .out(multiplexer_3_out), .sel(comparator_2_eq));
  Register #(.width(1)) register_5 (.D(or_4_out), .en(or_5_out), .clk(clk), .Q(UpdatedDirty));  // open: clr
  or or_6 (or_6_out, Byte1, Ways);
  or or_7 (or_7_out, Byte3, Ways);
  Multiplexer #(.enable("false"), .width(2)) multiplexer_4 (
    .in0(multiplexer_3_out), .in1(UpdatedAge), .out(multiplexer_4_out), .sel(comparator_2_gt));
  Demultiplexer #(.enable("false"), .select(2)) demultiplexer_1 (
    .out0(Byte0), .out1(Byte1), .out2(Byte2), .out3(Byte3), .in(Bytes), .sel(CpuAddress[1:0]));
  Register register_6 (.D(multiplexer_5_out), .en(or_6_out), .clk(clk), .Q(Line2Mem[15:8]));  // open: clr
  Multiplexer #(.enable("false"), .width(8)) multiplexer_5 (
    .in0(LineFromMemIn[15:8]), .in1(CpuWriteValueIn), .out(multiplexer_5_out), .sel(Bytes));
  Register register_7 (.D(multiplexer_6_out), .en(or_7_out), .clk(clk), .Q(Line2Mem[31:24]));  // open: clr
  Multiplexer #(.enable("false"), .width(8)) multiplexer_6 (
    .in0(LineFromMemIn[31:24]), .in1(CpuWriteValueIn), .out(multiplexer_6_out), .sel(Bytes));
  Multiplexer #(.enable("false"), .select(2), .width(8)) multiplexer_7 (
    .in0(Line2Mem[7:0]), .in1(Line2Mem[15:8]), .in2(Line2Mem[23:16]), .in3(Line2Mem[31:24]), .out(ByteRead),
    .sel(CpuAddress[1:0]));
  Multiplexer #(.enable("false"), .width(2)) multiplexer_8 (
    .in0(multiplexer_4_out), .in1(InitialAge), .out(multiplexer_8_out), .sel(Initialize));
  Register #(.width(1)) register_8 (.D(1'b1), .en(Ways), .clk(clk), .Q(UpdatedValid));  // open: clr

  // Other names for the same wires on the sheet: Ages_t[1:0] = NewAge; Offset[1:0] = CpuAddress[1:0];
  //   Set = CpuAddress[2]; Tag[6:0] = CpuAddress[9:3]; CpuWriteValue[7:0] = CpuWriteValueIn;
  //   UpdatedByte0[7:0] = Line2Mem[7:0]; UpdatedByte1[7:0] = Line2Mem[15:8]; UpdatedByte2[7:0] = Line2Mem[23:16];
  //   UpdatedByte3[7:0] = Line2Mem[31:24]; LineFromMem[31:0] = LineFromMemIn; Part0[7:0] = LineFromMemIn[7:0];
  //   Part1[7:0] = LineFromMemIn[15:8]; Part2[7:0] = LineFromMemIn[23:16]; Part3[7:0] = LineFromMemIn[31:24];
  //   NewAge_t = Ages
endmodule

module control (
  input  [9:0] CpuAddress,
  input  write,
  input  read,
  input  contain,
  input  dirty,
  input  clkIn,
  output [9:0] CpuAddressOut,
  output readyOut,
  output memReadOut,
  output memWriteOut,
  output initializationOut,
  output ContainOut,
  output age0Out,
  output age1Out,
  output line0Out,
  output line1Out,
  output byte0Out,
  output byte1Out
);

  wire fsm_1_newage, fsm_1_oneblock, fsm_1_onebyte, Read_t, readOut, readOutWriteOut, readWrite, S0, S1, S2,
       true, updateContain, Write_t, writeOut;
  wire [2:0] nextStep;

  fsm fsm_1 (
    .S0(S0), .S1(S1), .S2(S2), .read(Read_t), .write(Write_t), .contain(contain), .dirty(dirty),
    .ready(readyOut), .memRead(memReadOut), .Out2(nextStep[2]), .memWrite(memWriteOut),
    .initialization(initializationOut), .OneBlock(fsm_1_oneblock), .OneByte(fsm_1_onebyte),
    .Out0(nextStep[0]), .newContain(ContainOut), .newAge(fsm_1_newage), .Out1(nextStep[1]));
  Demultiplexer #(.enable("false")) demultiplexer_1 (
    .out0(byte0Out), .out1(byte1Out), .in(fsm_1_onebyte), .sel(CpuAddressOut[2]));
  Demultiplexer #(.enable("false")) demultiplexer_2 (
    .out0(line0Out), .out1(line1Out), .in(fsm_1_oneblock), .sel(CpuAddressOut[2]));
  Register #(.width(10)) register_1 (.D(CpuAddress), .en(readyOut), .clk(clkIn), .Q(CpuAddressOut));  // open: clr
  Demultiplexer #(.enable("false")) demultiplexer_3 (
    .out0(age0Out), .out1(age1Out), .in(fsm_1_newage), .sel(CpuAddressOut[2]));
  and and_1 (true, readWrite, readyOut);
  or or_1 (readWrite, read, write);
  Register #(.width(1)) register_2 (.D(read), .en(true), .clk(clkIn), .Q(readOut));  // open: clr
  Register #(.width(1)) register_3 (.D(write), .en(true), .clk(clkIn), .Q(writeOut));  // open: clr
  Multiplexer #(.enable("false")) multiplexer_1 (.in0(readOut), .in1(read), .out(Read_t), .sel(readyOut));
  Multiplexer #(.enable("false")) multiplexer_2 (.in0(writeOut), .in1(write), .out(Write_t), .sel(readyOut));
  Register #(.width(3)) register_4 (.D(nextStep), .clk(clkIn), .Q({S2, S1, S0}));  // open: en, clr
  or or_2 (readOutWriteOut, readOut, writeOut);
  and and_2 (updateContain, readOutWriteOut, ContainOut);

  // Other names for the same wires on the sheet: age0 = age0Out; age1 = age1Out; byte0 = byte0Out; byte1 = byte1Out;
  //   clk = clkIn; Contain_t = ContainOut; offSet[1:0] = CpuAddressOut[1:0]; sets = CpuAddressOut[2];
  //   tag[6:0] = CpuAddressOut[9:3]; initialization = initializationOut; line0 = line0Out; line1 = line1Out;
  //   memRead = memReadOut; memWrite = memWriteOut; ready = readyOut
endmodule

module set1 (
  input  [31:0] lineFromMem,
  input  [9:0] CpuAddressOut,
  input  [7:0] CpuWriteValue,
  input  initialize,
  input  age0,
  input  age1,
  input  line0,
  input  line1,
  input  byte0,
  input  byte1,
  input  clk,
  input  sets,
  output [6:0] Tag,
  output Dirty,
  output [31:0] Line2Mem,
  output [7:0] ByteRead,
  output Contain
);

  wire didContain0, didContain1, dirty0, dirty1;
  wire [6:0] tag0, tag1;
  wire [7:0] byteRead0, byteRead1;
  wire [31:0] line2Mem0, line2Mem1;

  Set set_1 (
    .CpuAddressOut(CpuAddressOut), .Initialize(initialize), .Ages(age0), .CpuWriteValueIn(CpuWriteValue),
    .LineFromMemIn(lineFromMem), .Ways(line0), .Bytes(byte0), .ClkIn(clk), .Tag(tag0), .Dirty(dirty0),
    .Line2Mem(line2Mem0), .ByteRead(byteRead0), .DidContain(didContain0));
  Set set_2 (
    .CpuAddressOut(CpuAddressOut), .Initialize(initialize), .Ages(age1), .CpuWriteValueIn(CpuWriteValue),
    .LineFromMemIn(lineFromMem), .Ways(line1), .Bytes(byte1), .ClkIn(clk), .Tag(tag1), .Dirty(dirty1),
    .Line2Mem(line2Mem1), .ByteRead(byteRead1), .DidContain(didContain1));
  Multiplexer #(.enable("false"), .width(7)) multiplexer_1 (.in0(tag0), .in1(tag1), .out(Tag), .sel(sets));
  Multiplexer #(.enable("false")) multiplexer_2 (.in0(dirty0), .in1(dirty1), .out(Dirty), .sel(sets));
  Multiplexer #(.enable("false"), .width(32)) multiplexer_3 (
    .in0(line2Mem0), .in1(line2Mem1), .out(Line2Mem), .sel(sets));
  Multiplexer #(.enable("false"), .width(8)) multiplexer_4 (
    .in0(byteRead0), .in1(byteRead1), .out(ByteRead), .sel(sets));
  Multiplexer #(.enable("false")) multiplexer_5 (.in0(didContain0), .in1(didContain1), .out(Contain), .sel(sets));
endmodule
